# Fritzing sketch schema (saved by Fritzing 0.9.5d)
breadboards: 2

parts:
  M1 = DOIT Esp32 DevKit v1 (30 pins long, 11 pins width) [part_number=ESP32S-PIN30]
  Компонент3 = Jtron 1 Channel Optoisolated Relay Module [package=relay]
  Компонент2 = RFID-RC522 [part_number=101218]
  LED1 = smd LED [color="Green (570nm)" package="1206 [SMD]"]
  R1 = Resistor [tolerance=±5% resistance=330 package="1206 [SMD]"]
  microSD1 = MicroSD Card Module  # not connected
  ZS-042_RTC1 = ZS-042 RTC Module  # not connected

nets:
  GND: M1.GND, Компонент3.GND, Компонент2.GND, LED1.cathode
  N1: M1.D4, R1.Pin_1
  N2: M1.D5, Компонент2.SDA
  N3: M1.D18, Компонент3.IN1
  N4: M1.D19, Компонент2.SCK
  N5: M1.D22, Компонент2.MISO
  N6: M1.D23, Компонент2.MOSI
  VIN: M1.VIN, Компонент3.VCC, Компонент2.IRQ
  N7: LED1.anode, R1.Pin_0

custom parts:
  DOIT Esp32 DevKit v1 (30 pins long, 11 pins width): The DOIT Esp32 DevKit v1 is one of the development board created by DOIT to evaluate the ESP-WROOM-32 module. It is based on the ESP32 microcontroller that boasts Wifi, Bluetooth, Ethernet and Low Power support all in a single chip. (vanepp) made breadboard work, adjusted pin numbering and labels and reduced size of schematic and cleaned up pcb. This chip is 30pins long (2 x15) and 11 pins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
